// Digital circuit ALU.dig as structural Verilog
module ALU (
  input  [31:0] A,
  input  [31:0] B,
  input  [2:0] OP,
  output [31:0] OUT,
  output Z
);

  wire comparator_1_eq, comparator_2_lt;
  wire [31:0] add_1_s, and_1_out, barrelshifter_1_out, bitextender_1_out, bitextender_2_out, or_1_out,
       sub_1_s, xor_1_out;

  Add #(.Bits(32)) add_1 (.a(A), .b(B), .c_i(1'b0), .s(add_1_s));  // open: c_o
  BarrelShifter #(.Bits(32), .barrelSigned("true")) barrelshifter_1 (.in(A), .shift(B[6:0]), .out(barrelshifter_1_out));
  Comparator #(.Bits(32)) comparator_1 (.a(A), .b(B), .eq(comparator_1_eq));  // open: gt, lt
  Comparator #(.Bits(32)) comparator_2 (.a(A), .b(B), .lt(comparator_2_lt));  // open: gt, eq
  assign xor_1_out = A ^ B;  // XOr xor_1, 32 bits wide
  Sub #(.Bits(32)) sub_1 (.a(A), .b(B), .c_i(1'b0), .s(sub_1_s));  // open: c_o
  assign or_1_out = A | B;  // Or or_1, 32 bits wide
  assign and_1_out = A & B;  // And and_1, 32 bits wide
  BitExtender #(.inputBits(1), .outputBits(32)) bitextender_1 (.in(comparator_1_eq), .out(bitextender_1_out));
  BitExtender #(.inputBits(1), .outputBits(32)) bitextender_2 (.in(comparator_2_lt), .out(bitextender_2_out));
  Multiplexer #(.Selector_Bits(3), .Bits(32)) multiplexer_1 (
    .sel(OP), .in_0(add_1_s), .in_1(barrelshifter_1_out), .in_2(bitextender_1_out), .in_3(bitextender_2_out),
    .in_4(xor_1_out), .in_5(sub_1_s), .in_6(or_1_out), .in_7(and_1_out), .out(OUT));
  Comparator #(.Bits(32)) comparator_3 (.a({32{1'b0}}), .b(OUT), .eq(Z));  // open: gt, lt
endmodule
