// Digital circuit CalcIMMopA.dig as structural Verilog
module CalcIMMopA (
  input  [31:0] opA,
  output [31:0] immA
);

  BitExtender #(.inputBits(20), .outputBits(32)) bitextender_1 (.in(opA[31:12]), .out(immA));
endmodule
