// Digital circuit PCsrc.dig as structural Verilog
module PCsrc (
  input  zero,
  input  IS,
  input  B,
  input  J,
  input  Jalr,
  output [1:0] PCsrc
);

  wire and_1_out, and_2_out;

  and and_1 (and_1_out, ~zero, ~IS, B);  // And
  and and_2 (and_2_out, zero, IS);
  or or_1 (PCsrc[0], and_1_out, and_2_out, J);

  assign PCsrc[1] = Jalr;

  // Other names for the same wires on the sheet: pc_src[1:0] = {Jalr, PCsrc[0]}
endmodule
