// Digital circuit Unidade de Controle.dig as structural Verilog
module Unidade_de_Controle (
  input  [31:0] E,
  output WREG,
  output [2:0] ULAop,
  output CI,
  output [1:0] REG,
  output WM,
  output [2:0] IMMop,
  output IS,
  output H,
  output jalr,
  output J,
  output B,
  output U
);

  wire I, R;

  unidade unidade_1 ();
  or or_1 (WREG, J, I, R);
  or or_2 (CI, WM, I);
  or or_3 (REG[1], J, jalr);

  // Other names for the same wires on the sheet: imm_op[2:0] = IMMop; lw = REG[0]; S = WM; ula_op[2:0] = ULAop
endmodule
