// Digital circuit calc imm.dig as structural Verilog
module calc_imm (
  input  [2:0] IMMop,
  input  [31:0] E,
  output [31:0] imm
);

  wire [31:0] bitextender_1_out, bitextender_2_out, bitextender_3_out, bitextender_4_out;

  BitExtender #(.inputBits(12), .outputBits(32)) bitextender_1 (.in(E[31:20]), .out(bitextender_1_out));
  BitExtender #(.inputBits(12), .outputBits(32)) bitextender_2 (.in({E[31:25], E[11:7]}), .out(bitextender_2_out));
  BitExtender #(.inputBits(13), .outputBits(32)) bitextender_3 (
    .in({E[31], E[7], E[30:25], E[11:8], 1'b0}), .out(bitextender_3_out));
  BitExtender #(.inputBits(21), .outputBits(32)) bitextender_4 (
    .in({E[31], E[19:12], E[20], E[30:21], 1'b0}), .out(bitextender_4_out));
  Multiplexer #(.Selector_Bits(3), .Bits(32)) multiplexer_1 (
    .sel(IMMop), .in_0(bitextender_1_out), .in_1(bitextender_2_out), .in_2(bitextender_3_out),
    .in_3(bitextender_4_out), .in_4(32'hc), .in_5(32'hc), .in_6(32'hc), .in_7(32'hc), .out(imm));
endmodule
