// Digital circuit processador.dig as structural Verilog
module processador (
  input  clk
);

  wire B, CI, comparator_1_eq, H, IS, J, jalr, multiplexer_2_out, U, WM, WREG, zero;
  wire [1:0] pcsrc_1_pcsrc, REG;
  wire [2:0] IMMop, ULAop;
  wire [31:0] A, add_2_s, alu_1_out, calc_imm_1_imm, calcimmopa_1_imma, MIout, multiplexer_6_out, not_1_out,
       opA, opB, pc_plus_4, PCactual, PCnext, ramdualport_1_d, Reg2Value, ULAout;

  // Probe on PCactual
  // Probe on PCnext
  // Probe on ULAout
  Multiplexer #(.Selector_Bits(2), .Bits(32)) multiplexer_1 (
    .sel(pcsrc_1_pcsrc), .in_0(pc_plus_4), .in_1(add_2_s), .in_2(ULAout), .in_3(ULAout), .out(PCnext));
  PCsrc pcsrc_1 (.zero(zero), .IS(IS), .B(B), .J(J), .Jalr(jalr), .PCsrc(pcsrc_1_pcsrc));
  Register #(.Bits(32), .isProgramCounter("true")) PC (.D(PCnext), .C(clk), .en(H), .Q(PCactual));
  Add #(.Bits(32)) add_1 (.a(PCactual), .b(32'h4), .c_i(1'b0), .s(pc_plus_4));  // open: c_o
  ROM #(.AddrBits(24), .Bits(32)) MI (.A(PCactual[23:0]), .sel(1'b1), .D(MIout));
  calc_imm calc_imm_1 (.IMMop(IMMop), .E(MIout), .imm(calc_imm_1_imm));
  Unidade_de_Controle unidade_de_controle_1 ();
  Comparator #(.Bits(5)) comparator_1 (.a({5{1'b0}}), .b(MIout[11:7]), .eq(comparator_1_eq));  // open: gt, lt
  Add #(.Bits(32)) add_2 (.a(PCactual), .b(calc_imm_1_imm), .c_i(1'b0), .s(add_2_s));  // open: c_o
  Multiplexer multiplexer_2 (.sel(comparator_1_eq), .in_0(WREG), .in_1(1'b0), .out(multiplexer_2_out));
  Banco_de_Registradores banco_de_registradores_1 (
    .CLK(clk), .WR(multiplexer_2_out), .WD(multiplexer_6_out), .RC(MIout[11:7]), .RA(MIout[19:15]),
    .RB(MIout[24:20]), .RS1(opA), .RS2(opB));
  CalcIMMopA calcimmopa_1 (.opA(MIout), .immA(calcimmopa_1_imma));
  Multiplexer #(.Bits(32)) multiplexer_3 (.sel(U), .in_0(opA), .in_1(calcimmopa_1_imma), .out(A));
  Multiplexer #(.Bits(32)) multiplexer_4 (.sel(CI), .in_0(opB), .in_1(calc_imm_1_imm), .out(Reg2Value));
  ALU alu_1 (.A(A), .B(Reg2Value), .OP(ULAop), .OUT(alu_1_out), .Z(zero));
  Multiplexer #(.Bits(32)) multiplexer_5 (.sel(IS), .in_0(alu_1_out), .in_1(not_1_out), .out(ULAout));
  assign not_1_out = ~alu_1_out;  // Not not_1, 32 bits wide
  Multiplexer #(.Selector_Bits(2), .Bits(32)) multiplexer_6 (
    .sel(REG), .in_0(ULAout), .in_1(ramdualport_1_d), .in_2(pc_plus_4), .in_3(pc_plus_4),
    .out(multiplexer_6_out));
  // Probe on ULAout
  RAMDualPort #(.AddrBits(24), .Bits(32)) ramdualport_1 (
    .A(ULAout[23:0]), .Din(opB), .str(WM), .C(clk), .ld(1'b1), .D(ramdualport_1_d));

  // Other names for the same wires on the sheet: clock = clk; Reg1Value[31:0] = A

  // Notes on the sheet:
  //   MI loads mod0.bin.hex
endmodule
