// Digital circuit unidade.dig as structural Verilog
module unidade (
  input  [6:0] opc,
  input  [2:0] f3,
  input  [6:0] f7,
  output J,
  output R,
  output S,
  output I,
  output B,
  output LW,
  output jalr,
  output IS,
  output [2:0] imm_op,
  output [2:0] ula_op,
  output U,
  output H
);

  wire and_3_out, and_4_out, and_5_out, and_6_out, and_7_out, and_8_out, and_9_out, and_10_out, and_11_out,
       and_12_out, and_13_out, and_14_out, and_15_out, and_16_out, and_17_out, and_18_out, and_19_out,
       and_20_out, and_24_out, and_30_out, and_31_out, I_sol, not_1_out, not_2_out;
  wire [0:0] or_3_out;
  wire [2:0] rom_1_d;

  not not_1 (not_1_out, opc[3]);
  not not_2 (not_2_out, opc[6]);
  and and_1 (imm_op[0], ~I, ~B);  // And
  and and_2 (imm_op[1], ~I, ~S);  // And
  and and_3 (and_3_out, opc[0], opc[1], opc[2]);
  and and_4 (and_4_out, opc[3], ~opc[4], opc[5], opc[6]);  // And
  and and_5 (and_5_out, opc[0], opc[1], ~opc[2]);  // And
  and and_6 (and_6_out, ~opc[3], opc[4], opc[5], ~opc[6]);  // And
  and and_7 (and_7_out, opc[0], opc[1], ~opc[2]);  // And
  and and_8 (and_8_out, ~opc[3], opc[4], ~opc[5], ~opc[6]);  // And
  and and_9 (and_9_out, opc[0], opc[1], ~opc[2]);  // And
  and and_10 (and_10_out, ~opc[3], ~opc[4], ~opc[5], ~opc[6]);  // And
  and and_11 (and_11_out, opc[0], opc[1], opc[2]);
  and and_12 (and_12_out, ~opc[3], ~opc[4], opc[5], opc[6]);  // And
  and and_13 (and_13_out, opc[0], opc[1], ~opc[2]);  // And
  and and_14 (and_14_out, ~opc[3], ~opc[4], opc[5], ~opc[6]);  // And
  and and_15 (and_15_out, opc[0], opc[1], ~opc[2]);  // And
  and and_16 (and_16_out, ~opc[3], ~opc[4], opc[5], opc[6]);  // And
  and and_17 (and_17_out, opc[2], not_1_out);
  and and_18 (and_18_out, opc[4], opc[5], not_2_out);
  and and_19 (and_19_out, ~opc[2], ~opc[3]);  // And
  and and_20 (and_20_out, opc[4], opc[5], opc[6]);
  and and_21 (S, and_13_out, and_14_out);
  and and_22 (B, and_15_out, and_16_out);
  and and_23 (imm_op[2], and_17_out, and_18_out);
  and and_24 (and_24_out, and_19_out, and_20_out);
  and and_25 (J, and_3_out, and_4_out);
  and and_26 (R, and_5_out, and_6_out);
  and and_27 (I_sol, and_7_out, and_8_out);
  and and_28 (LW, and_9_out, and_10_out);
  and and_29 (jalr, and_11_out, and_12_out);
  not not_3 (H, and_24_out);
  or or_1 (I, I_sol, LW, imm_op[2], jalr);
  and and_30 (and_30_out, B, f3[0], ~f3[1], ~f3[2]);  // And
  and and_31 (and_31_out, B, f3[0], ~f3[1], f3[2]);  // And
  or or_2 (IS, and_30_out, and_31_out);
  ROM #(.AddrBits(7), .isProgramMemory("true"), .Bits(3)) rom_1 (
    .A({imm_op[2], R, I_sol, f3, f7[5]}), .sel(1'b1), .D(rom_1_d));
  or or_3 (or_3_out[0], R, imm_op[2], I_sol);
  Multiplexer #(.Selector_Bits(2), .Bits(3)) multiplexer_1 (
    .sel({B, or_3_out[0]}), .in_0(3'b000), .in_1(rom_1_d), .in_2({2'b01, f3[2]}), .in_3({2'b01, f3[2]}),
    .out(ula_op));

  assign U = imm_op[2];

  // Other names for the same wires on the sheet: a0 = f3[0]; a1 = f3[1]; a2 = f3[2]; f7s = f7[5]; b0 = opc[0];
  //   b1 = opc[1]; b2 = opc[2]; b3 = opc[3]; b4 = opc[4]; b5 = opc[5]; b6 = opc[6]

  // Notes on the sheet:
  //   contents of rom_1 (hex, n*v repeats v):
  //   18*0,1,0,3,0,0,0,4,0,0,0,6,0,7,0,0,5,1,0,3,0,0,0,4,0,0,0,6,0,7
  //   ,31*0,1
endmodule
